# Fritzing sketch nRF52840-DK_PIR_IMU (saved by Fritzing 1.0.7)

parts:
  PPK1 = nordic PPK2 [mn=nordic mpn=nRF-PPK2 part_number=nRF-PPK2]
  M1 = nRF52 DK
  Bauteil1 = InvenSense MPU6050
  PIR1 = PIR sensor

nets:
  N1: PPK1.VOUT, M1.Pin_161
  N2: PPK1.GND#4, M1.Pin_159
  VCC: PPK1.VCC, M1.Pin_140, Bauteil1.VCC, PIR1.VDD
  GND: PPK1.GND#6, M1.Pin_117, M1.Pin_152, Bauteil1.GND, PIR1.GND
  N3: PPK1.D0, M1.Pin_91
  N4: M1.Pin_67, Bauteil1.SDA
  N5: M1.Pin_69, Bauteil1.SCL
  N6: M1.Pin_119, PIR1.SIG

custom parts:
  nordic PPK2: The Nordic Power Profiler Kit II
  nRF52 DK: The nRF52 DK is a versatile single board development kit for Bluetooth® Smart, ANT and 2.4GHz proprietary applications using the nRF52832 SoC. This kit supports development for the nRF52832 SoC. The kit is hardware compatible with the Arduino Uno Revision 3 standard, making it possible to use 3rd-party shields that are compatible to this standard. An NFC antenna can be connected the kit to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
